# Fritzing sketch Untitled Sketch (saved by Fritzing 0.9.4)

parts:
  ESP32_-_Back1 = ESP32 - CAM
  VCC1 = Battery
  M1 = Dagu DGServo 9g (Top view) [part_number=RS001B]
  M2 = Dagu DGServo 9g (Top view) [part_number=RS001B]

nets:
  N1: ESP32_-_Back1.GPIO14, M2.pulse
  N2: ESP32_-_Back1.GPIO15, M1.pulse
  GND: ESP32_-_Back1.GND, M1.gnd, M2.gnd
  N3: ESP32_-_Back1.5V, VCC1.+
  VCC: M1.vcc, M2.vcc

custom parts:
  ESP32 - CAM: The ESP32-CAM has a very competitive small-size camera module that can operate independently as a minimum system with a footprint of only 27*40.5*4.5mm and a deep sleep current of up to 6mA.
